# Fritzing sketch Prototype_Mega2560 (saved by Fritzing 0.7.12b)
breadboards: 2

parts:
  U1 = Arduino Mega
  Part1 = Arduino MicroSD Shield  # not connected
  LED3 = LED - 5mm [color="Green (555nm)" package="5 mm [THT]"]
  LED4 = LED - 5mm [color="Blue (470nm)" package="5 mm [THT]"]
  R1 = Resistor [tolerance=±5% resistance=220 package=THT]
  R2 = Resistor [tolerance=±5% resistance=220 package=THT]
  R3 = Resistor [tolerance=±5% resistance=220 package=THT]
  U5 = mystery part, 3 pins [chip_label=?]
  LED5 = LED - 5mm [color="Red (635nm)" package="5 mm [THT]"]
  LED2 = LED - 5mm [color="Orange (612nm)" package="5 mm [THT]"]
  R5 = Resistor [tolerance=±5% resistance=220 package=THT]
  U13 = mystery part, 3 pins [chip_label=?]
  U14 = mystery part, 3 pins [chip_label=?]
  U15 = mystery part, 3 pins [chip_label=?]
  S1 = Pushbutton [package="[THT]"]
  U16 = mystery part, 3 pins [chip_label=?]
  IC1 = DS1302 [package="SO8 [SMD]"]
  XTAL1 = CRYSTAL - kHz [frequency="32 kHz"]  # not connected
  Part2 = LilyPad Coin Cell Battery Holder

nets:
  N1: U1.D9, IC1.I/O_-_SPI_Data_In/Out
  N2: U1.D7, IC1.SCLK_-_SPI_Clock
  N3: U1.D3, U1.GND, U5.pin2, U13.pin2, U14.pin2, U15.pin2, S1.Pin_1, S1.Pin_2, S1.Pin_3, S1.Pin_4, U16.pin2, IC1.0V, Part2.-
  N4: U1.+5V, R1.Pin_1, R2.Pin_1, R3.Pin_1, U5.pin1, R5.Pin_1, U13.pin1, U14.pin1, U15.pin1, U16.pin1, IC1.+V
  N5: U1.A0, U15.pin3
  N6: U1.A1, U14.pin3
  N7: U1.A2, U13.pin3
  N8: U1.A3, U5.pin3
  N9: U1.A4, U16.pin3
  N10: U1.D46, LED5.cathode
  N11: U1.D47, LED2.cathode
  N12: U1.D48, LED3.cathode
  N13: U1.D49, LED4.anode, R2.Pin_0
  N14: LED3.anode, R1.Pin_0
  N15: R3.Pin_0, LED5.anode
  N16: LED2.anode, R5.Pin_0
  N17: IC1.Vbat_-_Backup_Supply, Part2.+

notes:
  Because Arduino Mega SPI is not wired to the same pins as Uno,
  Pins 8, 11, 12, 13 on SparkFun SD shield have to be bent
  (i.e. not connected to Arduino's one) and wrapped as follow:
  (CS) 8 -> 53
  (MOSI) 11 -> 51
  (MISO) 12 -> 50
  (SCK) 13 -> 52
  Differential pressure
  Absolute pressure
  Internal temperature
  External
  temperature
  Supply
  voltage
  HAO tracker protoype for Mega 2560
  ******************************
  v1.0 S.JEAN, 03/17/2013
  N.B. some items are not truly represented
  - DS1302 module is a breakout (DX sku126453)
  Sensors are not the definitive one but for testing purpose
  - Differential pressure is a raw MPX5100DP
  - Absolute pressure is a raw MPX5100A
  - internal an external temp. sensors are LM35
  - voltage sensor is a voltage divider (/2)
